// Logisim project NANDToCPU.circ as structural Verilog
module half_adder (
  input  in_1,
  input  in_2,
  output out_3,
  output out_4
);

  and and_1 (out_3, in_1, in_2);
  xor xor_1 (out_4, in_1, in_2);
endmodule

module Full_Adder (
  input  A,
  input  B,
  input  Carry,
  output C_Out,
  output Sum
);

  wire and_1_out, half_adder_1_out_3, half_adder_1_out_4;

  half_adder half_adder_1 (.in_1(B), .in_2(Carry), .out_3(half_adder_1_out_3), .out_4(half_adder_1_out_4));
  and and_1 (and_1_out, A, half_adder_1_out_4);
  xor xor_1 (Sum, A, half_adder_1_out_4);
  xor xor_2 (C_Out, and_1_out, half_adder_1_out_3);
endmodule

module _4_Bit_Adder (
  input  [3:0] in_1,
  input  [3:0] in_2,
  output out_3,
  output [3:0] out_4
);

  wire full_adder_1_c_out, full_adder_2_c_out, full_adder_3_c_out;

  Full_Adder full_adder_1 (.A(in_1[0]), .B(in_2[0]), .Carry(1'b0), .C_Out(full_adder_1_c_out), .Sum(out_4[0]));
  Full_Adder full_adder_2 (
    .A(in_1[1]), .B(in_2[1]), .Carry(full_adder_1_c_out), .C_Out(full_adder_2_c_out), .Sum(out_4[1]));
  Full_Adder full_adder_3 (
    .A(in_2[2]), .B(in_1[2]), .Carry(full_adder_2_c_out), .C_Out(full_adder_3_c_out), .Sum(out_4[2]));
  Full_Adder full_adder_4 (.A(in_2[3]), .B(in_1[3]), .Carry(full_adder_3_c_out), .C_Out(out_3), .Sum(out_4[3]));
endmodule

module _16_Bit_Adder__2 (
  input  in_1,
  input  [15:0] A,
  input  [15:0] B,
  output out_4,
  output [15:0] Sum
);

  wire full_adder_1_c_out, full_adder_2_c_out, full_adder_3_c_out, full_adder_4_c_out, full_adder_5_c_out,
       full_adder_6_c_out, full_adder_7_c_out, full_adder_8_c_out, full_adder_9_c_out, full_adder_10_c_out,
       full_adder_11_c_out, full_adder_12_c_out, full_adder_13_c_out, full_adder_14_c_out,
       full_adder_15_c_out;

  Full_Adder full_adder_1 (.A(A[0]), .B(B[0]), .Carry(in_1), .C_Out(full_adder_1_c_out), .Sum(Sum[0]));
  Full_Adder full_adder_2 (.A(A[1]), .B(B[1]), .Carry(full_adder_1_c_out), .C_Out(full_adder_2_c_out), .Sum(Sum[1]));
  Full_Adder full_adder_3 (.A(A[2]), .B(B[2]), .Carry(full_adder_2_c_out), .C_Out(full_adder_3_c_out), .Sum(Sum[2]));
  Full_Adder full_adder_4 (.A(A[3]), .B(B[3]), .Carry(full_adder_3_c_out), .C_Out(full_adder_4_c_out), .Sum(Sum[3]));
  Full_Adder full_adder_5 (.A(A[4]), .B(B[4]), .Carry(full_adder_4_c_out), .C_Out(full_adder_5_c_out), .Sum(Sum[4]));
  Full_Adder full_adder_6 (.A(A[5]), .B(B[5]), .Carry(full_adder_5_c_out), .C_Out(full_adder_6_c_out), .Sum(Sum[5]));
  Full_Adder full_adder_7 (.A(A[6]), .B(B[6]), .Carry(full_adder_6_c_out), .C_Out(full_adder_7_c_out), .Sum(Sum[6]));
  Full_Adder full_adder_8 (.A(A[7]), .B(B[7]), .Carry(full_adder_7_c_out), .C_Out(full_adder_8_c_out), .Sum(Sum[7]));
  Full_Adder full_adder_9 (.A(A[8]), .B(B[8]), .Carry(full_adder_8_c_out), .C_Out(full_adder_9_c_out), .Sum(Sum[8]));
  Full_Adder full_adder_10 (.A(A[9]), .B(B[9]), .Carry(full_adder_9_c_out), .C_Out(full_adder_10_c_out), .Sum(Sum[9]));
  Full_Adder full_adder_11 (
    .A(A[10]), .B(B[10]), .Carry(full_adder_10_c_out), .C_Out(full_adder_11_c_out), .Sum(Sum[10]));
  Full_Adder full_adder_12 (
    .A(A[11]), .B(B[11]), .Carry(full_adder_11_c_out), .C_Out(full_adder_12_c_out), .Sum(Sum[11]));
  Full_Adder full_adder_13 (
    .A(A[12]), .B(B[12]), .Carry(full_adder_12_c_out), .C_Out(full_adder_13_c_out), .Sum(Sum[12]));
  Full_Adder full_adder_14 (
    .A(A[13]), .B(B[13]), .Carry(full_adder_13_c_out), .C_Out(full_adder_14_c_out), .Sum(Sum[13]));
  Full_Adder full_adder_15 (
    .A(A[14]), .B(B[14]), .Carry(full_adder_14_c_out), .C_Out(full_adder_15_c_out), .Sum(Sum[14]));
  Full_Adder full_adder_16 (.A(A[15]), .B(B[15]), .Carry(full_adder_15_c_out), .C_Out(out_4), .Sum(Sum[15]));
endmodule

module Increment_16_Bit (
  input  [15:0] in_1,
  output [15:0] out_2,
  output out_3
);

  _16_Bit_Adder__2 u_16_bit_adder_2_1 (.Sum(out_2), .A(in_1), .B(16'h1), .out_4(out_3), .in_1(1'b0));
endmodule

module _16_Bit_Subtracter (
  input  [15:0] in_1,
  input  [15:0] in_2,
  output out_3,
  output [15:0] out_4
);

  wire increment_16_bit_1_out_3;
  wire [15:0] increment_16_bit_1_out_2, not_1_out;

  assign not_1_out = ~in_2;  // NOT_Gate not_1, 16 bits wide
  Increment_16_Bit increment_16_bit_1 (
    .in_1(not_1_out), .out_2(increment_16_bit_1_out_2), .out_3(increment_16_bit_1_out_3));
  _16_Bit_Adder__2 u_16_bit_adder_2_1 (
    .Sum(out_4), .A(in_1), .B(increment_16_bit_1_out_2), .out_4(out_3), .in_1(increment_16_bit_1_out_3));
endmodule

module _16_Bit_Equal_to_Zero (
  input  [15:0] in_1,
  output out_2
);

  wire or_1_out, or_2_out, or_3_out, or_4_out, or_5_out, or_6_out, or_7_out, or_8_out, or_9_out, or_10_out,
       or_11_out, or_12_out, or_13_out, or_14_out, or_15_out;

  or or_1 (or_1_out, in_1[0], in_1[1]);
  or or_2 (or_2_out, in_1[2], in_1[3]);
  or or_3 (or_3_out, in_1[4], in_1[5]);
  or or_4 (or_4_out, in_1[6], in_1[7]);
  or or_5 (or_5_out, in_1[8], in_1[9]);
  or or_6 (or_6_out, in_1[10], in_1[11]);
  or or_7 (or_7_out, in_1[12], in_1[13]);
  or or_8 (or_8_out, in_1[14], in_1[15]);
  or or_9 (or_9_out, or_1_out, or_2_out);
  or or_10 (or_10_out, or_3_out, or_4_out);
  or or_11 (or_11_out, or_5_out, or_6_out);
  or or_12 (or_12_out, or_7_out, or_8_out);
  or or_13 (or_13_out, or_9_out, or_10_out);
  or or_14 (or_14_out, or_11_out, or_12_out);
  or or_15 (or_15_out, or_13_out, or_14_out);
  not not_1 (out_2, or_15_out);
endmodule

module _16_Bit_Less_than_Zero (
  input  [15:0] in_1,
  output out_2
);


  assign out_2 = in_1[15];
endmodule

module Selector (
  input  Data_1,
  input  Data_0,
  input  Select,
  output Output
);

  wire and_1_out, and_2_out, not_1_out;

  not not_1 (not_1_out, Select);
  and and_1 (and_1_out, Data_1, Select);
  and and_2 (and_2_out, not_1_out, Data_0);
  or or_1 (Output, and_1_out, and_2_out);
endmodule

module Switch (
  input  Data,
  input  Select,
  output _1,
  output _0
);

  wire not_1_out;

  not not_1 (not_1_out, Select);
  and and_1 (_1, Data, Select);
  and and_2 (_0, Data, not_1_out);
endmodule

module Latch (
  input  Store,
  input  Data,
  output Output,
  output nOutput
);

  wire and_1_out, and_2_out, not_1_out;

  not not_1 (not_1_out, Data);
  and and_1 (and_1_out, not_1_out, Store);
  and and_2 (and_2_out, Store, Data);
  nor nor_1 (Output, and_1_out, nOutput);
  nor nor_2 (nOutput, Output, and_2_out);
endmodule

module Data_Flip_Flop (
  input  Store,
  input  Data,
  input  Clock,
  output out_4
);

  wire and_1_out, latch_1_output, not_1_out;

  not not_1 (not_1_out, Clock);
  Latch latch_1 (.Store(and_1_out), .Data(Data), .Output(latch_1_output));  // open: nOutput
  and and_1 (and_1_out, Store, not_1_out);
  Latch latch_2 (.Store(Clock), .Data(latch_1_output), .Output(out_4));  // open: nOutput
endmodule

module _2_Bit_Register (
  input  Data_1,
  input  Data_0,
  input  Store,
  output out_4,
  output out_5
);

  wire clock_1_out;

  Clock clock_1 (.out(clock_1_out));
  Data_Flip_Flop data_flip_flop_1 (.Store(Store), .Data(Data_1), .out_4(out_4), .Clock(clock_1_out));
  Data_Flip_Flop data_flip_flop_2 (.Store(Store), .Data(Data_0), .out_4(out_5), .Clock(clock_1_out));
endmodule

module _8_Bit_Register (
  input  [7:0] in_1,
  input  in_2,
  output [7:0] out_3
);

  wire clock_1_out;

  Clock clock_1 (.out(clock_1_out));
  Data_Flip_Flop data_flip_flop_1 (.Store(in_2), .Data(in_1[0]), .out_4(out_3[0]), .Clock(clock_1_out));
  Data_Flip_Flop data_flip_flop_2 (.Store(in_2), .Data(in_1[1]), .out_4(out_3[1]), .Clock(clock_1_out));
  Data_Flip_Flop data_flip_flop_3 (.Store(in_2), .Data(in_1[2]), .out_4(out_3[2]), .Clock(clock_1_out));
  Data_Flip_Flop data_flip_flop_4 (.Store(in_2), .Data(in_1[3]), .out_4(out_3[3]), .Clock(clock_1_out));
  Data_Flip_Flop data_flip_flop_5 (.Store(in_2), .Data(in_1[4]), .out_4(out_3[4]), .Clock(clock_1_out));
  Data_Flip_Flop data_flip_flop_6 (.Store(in_2), .Data(in_1[5]), .out_4(out_3[5]), .Clock(clock_1_out));
  Data_Flip_Flop data_flip_flop_7 (.Store(in_2), .Data(in_1[6]), .out_4(out_3[6]), .Clock(clock_1_out));
  Data_Flip_Flop data_flip_flop_8 (.Store(in_2), .Data(in_1[7]), .out_4(out_3[7]), .Clock(clock_1_out));
endmodule

module _16_Bit_Register (
  input  Store,
  input  Clock,
  input  [15:0] Input,
  output [15:0] Output
);

  D_Flip_Flop d_ff_1 (.clk(Clock), .D(Input[0]), .Q(Output[0]), .en(Store));  // open: Qn, preset, reset
  D_Flip_Flop d_ff_2 (.clk(Clock), .D(Input[1]), .Q(Output[1]), .en(Store));  // open: Qn, preset, reset
  D_Flip_Flop d_ff_3 (.clk(Clock), .D(Input[2]), .Q(Output[2]), .en(Store));  // open: Qn, preset, reset
  D_Flip_Flop d_ff_4 (.clk(Clock), .D(Input[3]), .Q(Output[3]), .en(Store));  // open: Qn, preset, reset
  D_Flip_Flop d_ff_5 (.clk(Clock), .D(Input[4]), .Q(Output[4]), .en(Store));  // open: Qn, preset, reset
  D_Flip_Flop d_ff_6 (.clk(Clock), .D(Input[5]), .Q(Output[5]), .en(Store));  // open: Qn, preset, reset
  D_Flip_Flop d_ff_7 (.clk(Clock), .D(Input[6]), .Q(Output[6]), .en(Store));  // open: Qn, preset, reset
  D_Flip_Flop d_ff_8 (.clk(Clock), .D(Input[7]), .Q(Output[7]), .en(Store));  // open: Qn, preset, reset
  D_Flip_Flop d_ff_9 (.clk(Clock), .D(Input[8]), .Q(Output[8]), .en(Store));  // open: Qn, preset, reset
  D_Flip_Flop d_ff_10 (.clk(Clock), .D(Input[9]), .Q(Output[9]), .en(Store));  // open: Qn, preset, reset
  D_Flip_Flop d_ff_11 (.clk(Clock), .D(Input[10]), .Q(Output[10]), .en(Store));  // open: Qn, preset, reset
  D_Flip_Flop d_ff_12 (.clk(Clock), .D(Input[11]), .Q(Output[11]), .en(Store));  // open: Qn, preset, reset
  D_Flip_Flop d_ff_13 (.clk(Clock), .D(Input[12]), .Q(Output[12]), .en(Store));  // open: Qn, preset, reset
  D_Flip_Flop d_ff_14 (.clk(Clock), .D(Input[13]), .Q(Output[13]), .en(Store));  // open: Qn, preset, reset
  D_Flip_Flop d_ff_15 (.clk(Clock), .D(Input[14]), .Q(Output[14]), .en(Store));  // open: Qn, preset, reset
  D_Flip_Flop d_ff_16 (.clk(Clock), .D(Input[15]), .Q(Output[15]), .en(Store));  // open: Qn, preset, reset
endmodule

module Counter (
  input  Clock,
  input  [15:0] Data,
  input  Store,
  output [15:0] Output
);

  wire not_1_out;
  wire [15:0] bitselector_1_out, increment_16_bit_1_out_2;

  Increment_16_Bit increment_16_bit_1 (.in_1(Output), .out_2(increment_16_bit_1_out_2));  // open: out_3
  BitSelector #(.width(32), .group(16)) bitselector_1 (
    .in({Data, increment_16_bit_1_out_2}), .out(bitselector_1_out), .sel(Store));
  not not_1 (not_1_out, Clock);
  _16_Bit_Register u_16_bit_register_1 (.Store(not_1_out), .Clock(Clock), .Input(bitselector_1_out), .Output(Output));
endmodule

module _2_Address_RAM (
  input  Store,
  input  [15:0] in_2,
  input  Address,
  input  Clock,
  output [15:0] out_5
);

  wire switch_1_p3, switch_1_p4;
  wire [15:0] n16_bit_register_1_output, n16_bit_register_2_output;

  // Switch switch_1: pin names not known; wires that end beside it: Store, Address, switch_1_p3, switch_1_p4
  _16_Bit_Register u_16_bit_register_1 (
    .Store(switch_1_p3), .Clock(Clock), .Input(in_2), .Output(n16_bit_register_1_output));
  _16_Bit_Register u_16_bit_register_2 (
    .Store(switch_1_p4), .Clock(Clock), .Input(in_2), .Output(n16_bit_register_2_output));
  BitSelector #(.width(32), .group(16)) bitselector_1 (
    .in({n16_bit_register_1_output, n16_bit_register_2_output}), .out(out_5), .sel(Address));
endmodule

module Unary_ALU (
  input  [15:0] X,
  input  Z,
  input  N,
  output [15:0] Output
);

  wire [15:0] bitselector_1_out, not_1_out;

  BitSelector #(.width(32), .group(16)) bitselector_1 (.in({{16{1'b0}}, X}), .out(bitselector_1_out), .sel(Z));
  assign not_1_out = ~bitselector_1_out;  // NOT_Gate not_1, 16 bits wide
  BitSelector #(.width(32), .group(16)) bitselector_2 (.in({not_1_out, bitselector_1_out}), .out(Output), .sel(N));
endmodule

module Full_ALU (
  input  [15:0] X,
  input  [15:0] Y,
  input  ZX,
  input  NX,
  input  ZY,
  input  NY,
  input  F,
  input  NO,
  output [15:0] Output
);

  wire [15:0] adder_1_out, and_1_out, bitselector_1_out, not_1_out, unary_alu_1_output, unary_alu_2_output;

  Unary_ALU unary_alu_1 (.X(X), .Z(ZX), .N(NX), .Output(unary_alu_1_output));
  Unary_ALU unary_alu_2 (.X(Y), .Z(ZY), .N(NY), .Output(unary_alu_2_output));
  assign and_1_out = unary_alu_1_output & unary_alu_2_output;  // AND_Gate and_1, 16 bits wide
  Adder #(.width(16)) adder_1 (
    .a(unary_alu_1_output), .b(unary_alu_2_output), .out(adder_1_out), .cin(1'b0));  // open: cout
  BitSelector #(.width(32), .group(16)) bitselector_1 (.in({adder_1_out, and_1_out}), .out(bitselector_1_out), .sel(F));
  assign not_1_out = ~bitselector_1_out;  // NOT_Gate not_1, 16 bits wide
  BitSelector #(.width(32), .group(16)) bitselector_2 (.in({not_1_out, bitselector_1_out}), .out(Output), .sel(NO));
endmodule

module Condition (
  input  Less_Than_0,
  input  Equal_to_0,
  input  Greater_Than_0,
  input  [15:0] Input,
  output out_5
);

  wire and_1_out, and_2_out, and_3_out, and_4_out, n16_bit_equal_to_zero_1_out_2,
       n16_bit_less_than_zero_1_out_2, not_1_out, not_2_out, or_1_out;

  _16_Bit_Equal_to_Zero u_16_bit_equal_to_zero_1 (.in_1(Input), .out_2(n16_bit_equal_to_zero_1_out_2));
  _16_Bit_Less_than_Zero u_16_bit_less_than_zero_1 (.in_1(Input), .out_2(n16_bit_less_than_zero_1_out_2));
  and and_1 (and_1_out, n16_bit_equal_to_zero_1_out_2, Equal_to_0);
  and and_2 (and_2_out, Greater_Than_0, not_1_out);
  not not_1 (not_1_out, n16_bit_equal_to_zero_1_out_2);
  or or_1 (or_1_out, and_1_out, and_3_out);
  and and_3 (and_3_out, n16_bit_less_than_zero_1_out_2, Less_Than_0);
  and and_4 (and_4_out, and_2_out, not_2_out);
  not not_2 (not_2_out, n16_bit_less_than_zero_1_out_2);
  or or_2 (out_5, or_1_out, and_4_out);
endmodule

module Combined_Memory (
  input  [15:0] Input,
  input  A,
  input  D,
  input  A_star,
  input  Clock,
  output [15:0] A_2,
  output [15:0] D_2,
  output [15:0] A_star_2
);

  _16_Bit_Register u_16_bit_register_1 (.Store(A), .Clock(Clock), .Input(Input), .Output(A_2));
  _16_Bit_Register u_16_bit_register_2 (.Store(D), .Clock(Clock), .Input(Input), .Output(D_2));
  _8_Byte_RAM u_8_byte_ram_1 (.Clock(Clock), .Store(A_star), .Input(Input), .Address(A_2[1:0]), .Output(A_star_2));
endmodule

module _8_Byte_RAM (
  input  Clock,
  input  Store,
  input  [15:0] Input,
  input  [1:0] Address,
  output [15:0] Output
);

  wire demultiplexer_1_out0, demultiplexer_1_out1, demultiplexer_1_out2, demultiplexer_1_out3;
  wire [15:0] n16_bit_register_1_output, n16_bit_register_2_output, n16_bit_register_3_output,
       n16_bit_register_4_output;

  Demultiplexer #(.select(2)) demultiplexer_1 (
    .out0(demultiplexer_1_out0), .out1(demultiplexer_1_out1), .out2(demultiplexer_1_out2),
    .out3(demultiplexer_1_out3), .in(Store), .sel(Address));  // open: en
  _16_Bit_Register u_16_bit_register_1 (
    .Store(demultiplexer_1_out0), .Clock(Clock), .Input(Input), .Output(n16_bit_register_1_output));
  _16_Bit_Register u_16_bit_register_2 (
    .Store(demultiplexer_1_out1), .Clock(Clock), .Input(Input), .Output(n16_bit_register_2_output));
  _16_Bit_Register u_16_bit_register_3 (
    .Store(demultiplexer_1_out2), .Clock(Clock), .Input(Input), .Output(n16_bit_register_3_output));
  _16_Bit_Register u_16_bit_register_4 (
    .Store(demultiplexer_1_out3), .Clock(Clock), .Input(Input), .Output(n16_bit_register_4_output));
  Multiplexer #(.select(2), .width(16)) multiplexer_1 (
    .in0(n16_bit_register_1_output), .in1(n16_bit_register_2_output), .in2(n16_bit_register_3_output),
    .in3(n16_bit_register_4_output), .out(Output), .sel(Address));  // open: en
endmodule

module Instruction_Decoder (
  input  [15:0] Input,
  output Ci,
  output Sm,
  output ZX,
  output NX,
  output ZY,
  output NY,
  output F,
  output No,
  output A,
  output D,
  output A_star,
  output GT,
  output EQ,
  output LT,
  output [15:0] W
);

  wire not_1_out;
  wire [15:5] multiplexer_1_out;

  Multiplexer #(.width(16)) multiplexer_1 (
    .in1(Input),
    .out({multiplexer_1_out[15:13], Sm, ZX, NX, ZY, NY, F, No, multiplexer_1_out[5], D, A_star, GT, EQ, LT}),
    .sel(Input[15]));  // open: in0, en
  not not_1 (not_1_out, Input[15]);
  or or_1 (A, multiplexer_1_out[5], not_1_out);
  Multiplexer #(.width(16)) multiplexer_2 (.in0(Input), .out(W), .sel(Input[15]));  // open: in1, en

  assign Ci = Input[15];
endmodule

module Control_Unit (
  input  [15:0] Instruction,
  input  CI,
  output [15:0] A,
  output J
);

  wire instruction_decoder_1_a, instruction_decoder_1_a_star, instruction_decoder_1_ci,
       instruction_decoder_1_d, instruction_decoder_1_eq, instruction_decoder_1_f, instruction_decoder_1_gt,
       instruction_decoder_1_lt, instruction_decoder_1_no, instruction_decoder_1_nx,
       instruction_decoder_1_ny, instruction_decoder_1_sm, instruction_decoder_1_zx, instruction_decoder_1_zy;
  wire [15:0] combined_memory_1_a_star_2, combined_memory_1_d_2, full_alu_1_output, instruction_decoder_1_w,
       multiplexer_1_out, multiplexer_2_out;

  Instruction_Decoder instruction_decoder_1 (
    .Input(Instruction), .Ci(instruction_decoder_1_ci), .Sm(instruction_decoder_1_sm),
    .ZX(instruction_decoder_1_zx), .NX(instruction_decoder_1_nx), .ZY(instruction_decoder_1_zy),
    .NY(instruction_decoder_1_ny), .F(instruction_decoder_1_f), .No(instruction_decoder_1_no),
    .A(instruction_decoder_1_a), .D(instruction_decoder_1_d), .A_star(instruction_decoder_1_a_star),
    .GT(instruction_decoder_1_gt), .EQ(instruction_decoder_1_eq), .LT(instruction_decoder_1_lt),
    .W(instruction_decoder_1_w));
  Multiplexer #(.width(16)) multiplexer_1 (
    .in0(A), .in1(combined_memory_1_a_star_2), .out(multiplexer_1_out), .sel(instruction_decoder_1_sm));  // open: en
  Multiplexer #(.width(16)) multiplexer_2 (
    .in0(instruction_decoder_1_w), .in1(full_alu_1_output), .out(multiplexer_2_out),
    .sel(instruction_decoder_1_ci));  // open: en
  Full_ALU full_alu_1 (
    .X(combined_memory_1_d_2), .Y(multiplexer_1_out), .ZX(instruction_decoder_1_zx),
    .NX(instruction_decoder_1_nx), .ZY(instruction_decoder_1_zy), .NY(instruction_decoder_1_ny),
    .F(instruction_decoder_1_f), .NO(instruction_decoder_1_no), .Output(full_alu_1_output));
  Combined_Memory combined_memory_1 (
    .Input(multiplexer_2_out), .A(instruction_decoder_1_a), .D(instruction_decoder_1_d),
    .A_star(instruction_decoder_1_a_star), .Clock(CI), .A_2(A), .D_2(combined_memory_1_d_2),
    .A_star_2(combined_memory_1_a_star_2));
  Condition condition_1 (
    .Less_Than_0(instruction_decoder_1_eq), .Equal_to_0(instruction_decoder_1_lt),
    .Greater_Than_0(instruction_decoder_1_gt), .Input(full_alu_1_output), .out_5(J));
endmodule

module Program_Engine (
  input  Jump,
  input  [15:0] Address,
  input  Clock,
  output [15:0] out_4
);

  wire [15:0] counter_1_output;

  Counter counter_1 (.Clock(Clock), .Data(Address), .Store(Jump), .Output(counter_1_output));
  ROM #(.addrWidth(16), .dataWidth(16)) rom_1 (.addr(counter_1_output), .data(out_4));  // open: sel
endmodule
