// Logisim project CustomCPU.circ as structural Verilog
module ALU (
  input  [31:0] X,
  input  [31:0] Y,
  input  Zero_X,
  input  Invert_X,
  input  Zero_Y,
  input  Invert_Y,
  input  AND___ADD,
  input  Invert_Output,
  output [31:0] ALU_Output
);

  wire [31:0] adder_1_out, and_1_out, multiplexer_1_out, not_1_out, single_alu_1_out_4, single_alu_2_out_4;

  Single_ALU single_alu_1 (.Zero(Zero_X), .Invert(Invert_X), .Input(X), .out_4(single_alu_1_out_4));
  Single_ALU single_alu_2 (.Zero(Zero_Y), .Invert(Invert_Y), .Input(Y), .out_4(single_alu_2_out_4));
  Adder #(.width(32)) adder_1 (.a(single_alu_1_out_4), .b(single_alu_2_out_4), .out(adder_1_out));  // open: cin, cout
  assign and_1_out = single_alu_1_out_4 & single_alu_2_out_4;  // AND_Gate and_1, 32 bits wide
  Multiplexer #(.width(32)) multiplexer_1 (
    .in0(and_1_out), .in1(adder_1_out), .out(multiplexer_1_out), .sel(AND___ADD));  // open: en
  assign not_1_out = ~multiplexer_1_out;  // NOT_Gate not_1, 32 bits wide
  Multiplexer #(.width(32)) multiplexer_2 (
    .in0(multiplexer_1_out), .in1(not_1_out), .out(ALU_Output), .sel(Invert_Output));  // open: en

  // Notes on the sheet:
  //   Zero Y, Invert Y, ADD to subtract ONE
  //   No modifier to AND X/Y
  //   Invert X, ADD, Invert Output for X - Y
endmodule

module Single_ALU (
  input  Zero,
  input  Invert,
  input  [31:0] Input,
  output [31:0] out_4
);

  wire [31:0] multiplexer_1_out, not_1_out;

  Multiplexer #(.width(32)) multiplexer_1 (
    .in0(Input), .in1({32{1'b0}}), .out(multiplexer_1_out), .sel(Zero));  // open: en
  assign not_1_out = ~multiplexer_1_out;  // NOT_Gate not_1, 32 bits wide
  Multiplexer #(.width(32)) multiplexer_2 (
    .in0(multiplexer_1_out), .in1(not_1_out), .out(out_4), .sel(Invert));  // open: en
endmodule

module Condition (
  input  [31:0] Input,
  input  [31:0] Comparator,
  input  Not_Equal,
  input  Equal,
  input  Greater_Than,
  input  Less_Than,
  output out_7
);

  wire and_1_out, and_2_out, and_3_out, and_4_out, comparator_1_eq, comparator_1_gt, comparator_1_lt,
       not_1_out;

  Comparator #(.width(32)) comparator_1 (
    .a(Input), .b(Comparator), .gt(comparator_1_gt), .eq(comparator_1_eq), .lt(comparator_1_lt));
  not not_1 (not_1_out, comparator_1_eq);
  and and_1 (and_1_out, Not_Equal, not_1_out);
  and and_2 (and_2_out, comparator_1_eq, Equal);
  and and_3 (and_3_out, comparator_1_gt, Greater_Than);
  and and_4 (and_4_out, comparator_1_lt, Less_Than);
  or or_1 (out_7, and_1_out, and_2_out, and_3_out, and_4_out);
endmodule

module Instruction_Decoder (
  input  [31:0] Input,
  output ZeroX,
  output InvertX,
  output ZeroY,
  output InvertY,
  output AND___ADD,
  output Invert_Output,
  output [4:0] SRC1,
  output [4:0] SRC2,
  output [4:0] DEST,
  output SRC1_Type,
  output SRC2_Type,
  output DEST_Type,
  output Jump_If_Not_Equal,
  output Jump_If_Equal,
  output Jump_if_Less_Than,
  output Jump_if_Greater_Than,
  output Comparator_Type
);


  assign AND___ADD = Input[4];
  assign Comparator_Type = Input[28];
  assign DEST = Input[20:16];
  assign DEST_Type = Input[23];
  assign Invert_Output = Input[5];
  assign InvertX = Input[1];
  assign InvertY = Input[3];
  assign Jump_If_Equal = Input[25];
  assign Jump_if_Greater_Than = Input[27];
  assign Jump_if_Less_Than = Input[26];
  assign Jump_If_Not_Equal = Input[24];
  assign SRC1 = Input[10:6];
  assign SRC1_Type = Input[21];
  assign SRC2 = Input[15:11];
  assign SRC2_Type = Input[22];
  assign ZeroX = Input[0];
  assign ZeroY = Input[2];
endmodule

module Control_Unit (
  input  Clear,
  input  [31:0] Input,
  input  Clock,
  output Jump,
  output [31:0] ARAM_Register,
  output [31:0] JMP_Register
);

  wire instruction_decoder_1_and___add, instruction_decoder_1_comparator_type,
       instruction_decoder_1_dest_type, instruction_decoder_1_invert_output, instruction_decoder_1_invertx,
       instruction_decoder_1_inverty, instruction_decoder_1_jump_if_equal,
       instruction_decoder_1_jump_if_greater_than, instruction_decoder_1_jump_if_less_than,
       instruction_decoder_1_jump_if_not_equal, instruction_decoder_1_src1_type,
       instruction_decoder_1_src2_type, instruction_decoder_1_zerox, instruction_decoder_1_zeroy, not_1_out,
       not_2_out;
  wire [4:0] instruction_decoder_1_dest, instruction_decoder_1_src1, instruction_decoder_1_src2;
  wire [31:0] alu_1_alu_output, combined_memory_v2_1_a, combined_memory_v2_1_b, combined_memory_v2_1_c,
       combined_memory_v2_1_d, combined_memory_v2_1_e, combined_memory_v2_1_exa0, combined_memory_v2_1_exa1,
       combined_memory_v2_1_exp0, combined_memory_v2_1_exp0_2, combined_memory_v2_1_exp1,
       combined_memory_v2_1_exr0, combined_memory_v2_1_exr1, combined_memory_v2_1_exw0,
       combined_memory_v2_1_exw1, combined_memory_v2_1_f, combined_memory_v2_1_g, combined_memory_v2_1_h,
       combined_memory_v2_1_i, combined_memory_v2_1_ndin0, combined_memory_v2_1_ndin1,
       combined_memory_v2_1_ndout0, combined_memory_v2_1_ndout1, combined_memory_v2_1_nmin0,
       combined_memory_v2_1_nmin1, combined_memory_v2_1_nmout0, combined_memory_v2_1_nmout1,
       combined_memory_v2_1_npin0, combined_memory_v2_1_npout0, combined_memory_v2_1_npout1,
       combined_memory_v2_1_ram, multiplexer_1_out, multiplexer_2_out, multiplexer_3_out, multiplexer_4_out,
       multiplexer_5_out;

  not not_1 (not_1_out, Clear);
  Instruction_Decoder instruction_decoder_1 (
    .Input(Input), .ZeroX(instruction_decoder_1_zerox), .InvertX(instruction_decoder_1_invertx),
    .ZeroY(instruction_decoder_1_zeroy), .InvertY(instruction_decoder_1_inverty),
    .AND___ADD(instruction_decoder_1_and___add), .Invert_Output(instruction_decoder_1_invert_output),
    .SRC1(instruction_decoder_1_src1), .SRC2(instruction_decoder_1_src2), .DEST(instruction_decoder_1_dest),
    .SRC1_Type(instruction_decoder_1_src1_type), .SRC2_Type(instruction_decoder_1_src2_type),
    .DEST_Type(instruction_decoder_1_dest_type), .Jump_If_Not_Equal(instruction_decoder_1_jump_if_not_equal),
    .Jump_If_Equal(instruction_decoder_1_jump_if_equal),
    .Jump_if_Less_Than(instruction_decoder_1_jump_if_less_than),
    .Jump_if_Greater_Than(instruction_decoder_1_jump_if_greater_than),
    .Comparator_Type(instruction_decoder_1_comparator_type));
  not not_2 (not_2_out, instruction_decoder_1_dest_type);
  Combined_Memory_v2 combined_memory_v2_1 (
    .Clear(not_1_out), .Clock(Clock), .Store(not_2_out), .Select(instruction_decoder_1_dest),
    .Input(alu_1_alu_output), .JMP(JMP_Register), .NDIN0(combined_memory_v2_1_ndin0),
    .RAM(combined_memory_v2_1_ram), .A(combined_memory_v2_1_a), .NPIN0(combined_memory_v2_1_npin0),
    .B(combined_memory_v2_1_b), .NMIN0(combined_memory_v2_1_nmin0), .C(combined_memory_v2_1_c),
    .NDOUT1(combined_memory_v2_1_ndout1), .D(combined_memory_v2_1_d), .NPOUT1(combined_memory_v2_1_npout1),
    .NDOUT0(combined_memory_v2_1_ndout0), .NMOUT1(combined_memory_v2_1_nmout1),
    .NPOUT0(combined_memory_v2_1_npout0), .NDIN1(combined_memory_v2_1_ndin1),
    .NMOUT0(combined_memory_v2_1_nmout0), .NMIN1(combined_memory_v2_1_nmin1),
    .EXP1(combined_memory_v2_1_exp1), .E(combined_memory_v2_1_e), .F(combined_memory_v2_1_f),
    .G(combined_memory_v2_1_g), .H(combined_memory_v2_1_h), .I(combined_memory_v2_1_i),
    .EXA0(combined_memory_v2_1_exa0), .EXW0(combined_memory_v2_1_exw0), .EXR0(combined_memory_v2_1_exr0),
    .EXP0(combined_memory_v2_1_exp0), .EXP0_2(combined_memory_v2_1_exp0_2), .EXA1(combined_memory_v2_1_exa1),
    .EXW1(combined_memory_v2_1_exw1), .EXR1(combined_memory_v2_1_exr1), .ARAM(ARAM_Register));
  Multiplexer #(.select(5), .width(32)) multiplexer_1 (
    .in0(combined_memory_v2_1_ram), .in1(ARAM_Register), .in2(JMP_Register), .in3(combined_memory_v2_1_a),
    .in4(combined_memory_v2_1_b), .in5(combined_memory_v2_1_c), .in6(combined_memory_v2_1_d),
    .in7(combined_memory_v2_1_ndout0), .in8(combined_memory_v2_1_npout0), .in9(combined_memory_v2_1_nmout0),
    .in10(combined_memory_v2_1_ndin0), .in11(combined_memory_v2_1_npin0), .in12(combined_memory_v2_1_nmin0),
    .in13(combined_memory_v2_1_ndout1), .in14(combined_memory_v2_1_npout1),
    .in15(combined_memory_v2_1_nmout1), .in16(combined_memory_v2_1_ndin1), .in17(combined_memory_v2_1_nmin1),
    .in18(combined_memory_v2_1_exp1), .in19(combined_memory_v2_1_exa0), .in20(combined_memory_v2_1_exw0),
    .in21(combined_memory_v2_1_exr0), .in22(combined_memory_v2_1_exp0), .in23(combined_memory_v2_1_exp0_2),
    .in24(combined_memory_v2_1_exa1), .in25(combined_memory_v2_1_exw1), .in26(combined_memory_v2_1_exr1),
    .in27(combined_memory_v2_1_e), .in28(combined_memory_v2_1_f), .in29(combined_memory_v2_1_g),
    .in30(combined_memory_v2_1_h), .in31(combined_memory_v2_1_i), .out(multiplexer_1_out),
    .sel(instruction_decoder_1_src2));  // open: en
  Multiplexer #(.select(5), .width(32)) multiplexer_2 (
    .in0(combined_memory_v2_1_ram), .in1(ARAM_Register), .in2(JMP_Register), .in3(combined_memory_v2_1_a),
    .in4(combined_memory_v2_1_b), .in5(combined_memory_v2_1_c), .in6(combined_memory_v2_1_d),
    .in7(combined_memory_v2_1_ndout0), .in8(combined_memory_v2_1_npout0), .in9(combined_memory_v2_1_nmout0),
    .in10(combined_memory_v2_1_ndin0), .in11(combined_memory_v2_1_npin0), .in12(combined_memory_v2_1_nmin0),
    .in13(combined_memory_v2_1_ndout1), .in14(combined_memory_v2_1_npout1),
    .in15(combined_memory_v2_1_nmout1), .in16(combined_memory_v2_1_ndin1), .in17(combined_memory_v2_1_nmin1),
    .in18(combined_memory_v2_1_exp1), .in19(combined_memory_v2_1_exa0), .in20(combined_memory_v2_1_exw0),
    .in21(combined_memory_v2_1_exr0), .in22(combined_memory_v2_1_exp0), .in23(combined_memory_v2_1_exp0_2),
    .in24(combined_memory_v2_1_exa1), .in25(combined_memory_v2_1_exw1), .in26(combined_memory_v2_1_exr1),
    .in27(combined_memory_v2_1_e), .in28(combined_memory_v2_1_f), .in29(combined_memory_v2_1_g),
    .in30(combined_memory_v2_1_h), .in31(combined_memory_v2_1_i), .out(multiplexer_2_out),
    .sel(instruction_decoder_1_src1));  // open: en
  Multiplexer #(.width(32)) multiplexer_3 (
    .in0(multiplexer_1_out), .in1({{27{1'b0}}, instruction_decoder_1_src1}), .out(multiplexer_3_out),
    .sel(instruction_decoder_1_src2_type));  // open: en
  Multiplexer #(.width(32)) multiplexer_4 (
    .in0(multiplexer_2_out), .in1({{27{1'b0}}, instruction_decoder_1_src2}), .out(multiplexer_4_out),
    .sel(instruction_decoder_1_src1_type));  // open: en
  Multiplexer #(.width(32)) multiplexer_5 (
    .in0({{27{1'b0}}, instruction_decoder_1_src1}), .in1(multiplexer_1_out), .out(multiplexer_5_out),
    .sel(instruction_decoder_1_comparator_type));  // open: en
  ALU alu_1 (
    .X(multiplexer_4_out), .Y(multiplexer_3_out), .Zero_X(instruction_decoder_1_zerox),
    .Invert_X(instruction_decoder_1_invertx), .Zero_Y(instruction_decoder_1_zeroy),
    .Invert_Y(instruction_decoder_1_inverty), .AND___ADD(instruction_decoder_1_and___add),
    .Invert_Output(instruction_decoder_1_invert_output), .ALU_Output(alu_1_alu_output));
  Condition condition_1 (
    .Input(multiplexer_4_out), .Comparator(multiplexer_5_out),
    .Not_Equal(instruction_decoder_1_jump_if_not_equal), .Equal(instruction_decoder_1_jump_if_equal),
    .Greater_Than(instruction_decoder_1_jump_if_less_than),
    .Less_Than(instruction_decoder_1_jump_if_greater_than), .out_7(Jump));

  // Notes on the sheet:
  //   SRC2
  //   SRC1
  //   uuugggggggg
endmodule

module Combined_Memory_v2 (
  input  Clear,
  input  Clock,
  input  Store,
  input  [4:0] Select,
  input  [31:0] Input,
  output [31:0] ARAM,
  output [31:0] JMP,
  output [31:0] NDIN0,
  output [31:0] RAM,
  output [31:0] A,
  output [31:0] NPIN0,
  output [31:0] B,
  output [31:0] NMIN0,
  output [31:0] C,
  output [31:0] NDOUT1,
  output [31:0] D,
  output [31:0] NPOUT1,
  output [31:0] NDOUT0,
  output [31:0] NMOUT1,
  output [31:0] NPOUT0,
  output [31:0] NDIN1,
  output [31:0] NMOUT0,
  output [31:0] NMIN1,
  output [31:0] EXA0,
  output [31:0] EXW0,
  output [31:0] EXR0,
  output [31:0] EXP0,
  output [31:0] EXP0_2,
  output [31:0] EXA1,
  output [31:0] EXW1,
  output [31:0] EXR1,
  output [31:0] EXP1,
  output [31:0] E,
  output [31:0] F,
  output [31:0] G,
  output [31:0] H,
  output [31:0] I
);

  wire and_1_out, demultiplexer_1_out0, demultiplexer_1_out1, demultiplexer_1_out2, demultiplexer_1_out3,
       demultiplexer_1_out4, demultiplexer_1_out5, demultiplexer_1_out6, demultiplexer_1_out7,
       demultiplexer_1_out8, demultiplexer_1_out9, demultiplexer_1_out10, demultiplexer_1_out11,
       demultiplexer_1_out12, demultiplexer_1_out13, demultiplexer_1_out14, demultiplexer_1_out15,
       demultiplexer_1_out16, demultiplexer_1_out17, demultiplexer_1_out18, demultiplexer_1_out19,
       demultiplexer_1_out20, demultiplexer_1_out21, demultiplexer_1_out22, demultiplexer_1_out23,
       demultiplexer_1_out24, demultiplexer_1_out25, demultiplexer_1_out26, demultiplexer_1_out27,
       demultiplexer_1_out28, demultiplexer_1_out29, demultiplexer_1_out30, demultiplexer_1_out31;
  wire [31:0] undriven;

  Demultiplexer #(.select(5)) demultiplexer_1 (
    .out0(demultiplexer_1_out0), .out1(demultiplexer_1_out1), .out2(demultiplexer_1_out2),
    .out3(demultiplexer_1_out3), .out4(demultiplexer_1_out4), .out5(demultiplexer_1_out5),
    .out6(demultiplexer_1_out6), .out7(demultiplexer_1_out7), .out8(demultiplexer_1_out8),
    .out9(demultiplexer_1_out9), .out10(demultiplexer_1_out10), .out11(demultiplexer_1_out11),
    .out12(demultiplexer_1_out12), .out13(demultiplexer_1_out13), .out14(demultiplexer_1_out14),
    .out15(demultiplexer_1_out15), .out16(demultiplexer_1_out16), .out17(demultiplexer_1_out17),
    .out18(demultiplexer_1_out18), .out19(demultiplexer_1_out19), .out20(demultiplexer_1_out20),
    .out21(demultiplexer_1_out21), .out22(demultiplexer_1_out22), .out23(demultiplexer_1_out23),
    .out24(demultiplexer_1_out24), .out25(demultiplexer_1_out25), .out26(demultiplexer_1_out26),
    .out27(demultiplexer_1_out27), .out28(demultiplexer_1_out28), .out29(demultiplexer_1_out29),
    .out30(demultiplexer_1_out30), .out31(demultiplexer_1_out31), .in(and_1_out), .sel(Select));  // open: en
  and and_1 (and_1_out, Store, 1'b1);
  RAM #(.dataWidth(32), .bus("separate")) ram_1 (
    .addr(ARAM[7:0]), .din(Input), .data(RAM), .str(demultiplexer_1_out0), .clk(Clock), .ld(1'b1), .clr(Clear));  // open: sel
  Register #(.width(32)) u_B (.D(undriven), .en(demultiplexer_1_out4), .Q(B), .clk(Clock), .clr(Clear));
  Register #(.width(32)) u_NPOUT0 (.D(undriven), .en(demultiplexer_1_out8), .Q(NPOUT0), .clk(Clock), .clr(Clear));
  Register #(.width(32)) u_NMIN0 (.D(undriven), .en(demultiplexer_1_out12), .Q(NMIN0), .clk(Clock), .clr(Clear));
  Register #(.width(32)) u_NDIN1 (.D(undriven), .en(demultiplexer_1_out16), .Q(NDIN1), .clk(Clock), .clr(Clear));
  Register #(.width(32)) u_EXW0 (.D(undriven), .en(demultiplexer_1_out20), .Q(EXR0), .clk(Clock), .clr(Clear));
  Register #(.width(32)) u_EXW1 (.D(undriven), .en(demultiplexer_1_out24), .Q(EXW1), .clk(Clock), .clr(Clear));
  Register #(.width(32)) u_F (.D(undriven), .en(demultiplexer_1_out28), .Q(F), .clk(Clock), .clr(Clear));
  Register #(.width(32)) u_ARAM (.D(Input), .en(demultiplexer_1_out1), .Q(ARAM), .clk(Clock), .clr(Clear));
  Register #(.width(32)) u_C (.D(Input), .en(demultiplexer_1_out5), .Q(C), .clk(Clock), .clr(Clear));
  Register #(.width(32)) u_NMOUT0 (.D(Input), .en(demultiplexer_1_out9), .Q(NMOUT0), .clk(Clock), .clr(Clear));
  Register #(.width(32)) u_NDOUT1 (.D(Input), .en(demultiplexer_1_out13), .Q(NDOUT1), .clk(Clock), .clr(Clear));
  Register #(.width(32)) NPIN1 (.D(Input), .en(demultiplexer_1_out17), .Q(NMIN1), .clk(Clock), .clr(Clear));
  Register #(.width(32)) u_EXR0 (.D(Input), .en(demultiplexer_1_out21), .Q(EXP0), .clk(Clock), .clr(Clear));
  Register #(.width(32)) u_EXR1 (.D(Input), .en(demultiplexer_1_out25), .Q(EXR1), .clk(Clock), .clr(Clear));
  Register #(.width(32)) u_G (.D(Input), .en(demultiplexer_1_out29), .Q(G), .clk(Clock), .clr(Clear));
  Register #(.width(32)) u_JMP (.D(Input), .en(demultiplexer_1_out2), .Q(JMP), .clk(Clock), .clr(Clear));
  Register #(.width(32)) u_D (.D(Input), .en(demultiplexer_1_out6), .Q(D), .clk(Clock), .clr(Clear));
  Register #(.width(32)) u_NDIN0 (.D(Input), .en(demultiplexer_1_out10), .Q(NDIN0), .clk(Clock), .clr(Clear));
  Register #(.width(32)) u_NPOUT1 (.D(Input), .en(demultiplexer_1_out14), .Q(NPOUT1), .clk(Clock), .clr(Clear));
  Register #(.width(32)) u_NMIN1 (.D(Input), .en(demultiplexer_1_out18), .Q(EXA0), .clk(Clock), .clr(Clear));
  Register #(.width(32)) u_EXP0 (.D(Input), .en(demultiplexer_1_out22), .Q(EXP0_2), .clk(Clock), .clr(Clear));
  Register #(.width(32)) u_EXP1 (.D(Input), .en(demultiplexer_1_out26), .Q(EXP1), .clk(Clock), .clr(Clear));
  Register #(.width(32)) u_H (.D(Input), .en(demultiplexer_1_out30), .Q(H), .clk(Clock), .clr(Clear));
  Register #(.width(32)) u_A (.D(Input), .en(demultiplexer_1_out3), .Q(A), .clk(Clock), .clr(Clear));
  Register #(.width(32)) u_NDOUT0 (.D(Input), .en(demultiplexer_1_out7), .Q(NDOUT0), .clk(Clock), .clr(Clear));
  Register #(.width(32)) u_NPIN0 (.D(Input), .en(demultiplexer_1_out11), .Q(NPIN0), .clk(Clock), .clr(Clear));
  Register #(.width(32)) u_NMOUT1 (.D(Input), .en(demultiplexer_1_out15), .Q(NMOUT1), .clk(Clock), .clr(Clear));
  Register #(.width(32)) u_EXA0 (.D(Input), .en(demultiplexer_1_out19), .Q(EXW0), .clk(Clock), .clr(Clear));
  Register #(.width(32)) u_EXA1 (.D(Input), .en(demultiplexer_1_out23), .Q(EXA1), .clk(Clock), .clr(Clear));
  Register #(.width(32)) u_E (.D(Input), .en(demultiplexer_1_out27), .Q(E), .clk(Clock), .clr(Clear));
  Register #(.width(32)) u_I (.D(Input), .en(demultiplexer_1_out31), .Q(I), .clk(Clock), .clr(Clear));
endmodule

module Executor (
  input  ManualJump,
  input  On_Off,
  input  [1:0] ROM_Select,
  output [31:0] out_4
);

  wire clock_1_out, control_unit_1_jump, demultiplexer_1_out0, demultiplexer_1_out1, demultiplexer_1_out2,
       demultiplexer_1_out3, or_1_out;
  wire [31:0] control_unit_1_jmp_register, counter_1_out_4, rom_1_data, rom_2_data, rom_3_data, rom_4_data;

  Clock clock_1 (.out(clock_1_out));
  or or_1 (or_1_out, ManualJump, control_unit_1_jump);
  Demultiplexer #(.select(2)) demultiplexer_1 (
    .out0(demultiplexer_1_out0), .out1(demultiplexer_1_out1), .out2(demultiplexer_1_out2),
    .out3(demultiplexer_1_out3), .in(On_Off), .sel(ROM_Select), .en(1'b1));
  Counter counter_1 (
    .Clock(clock_1_out), .Store(or_1_out), .in_3(control_unit_1_jmp_register), .out_4(counter_1_out_4));
  ROM #(.addrWidth(5), .dataWidth(32)) rom_1 (
    .addr(counter_1_out_4[4:0]), .data(rom_1_data), .sel(demultiplexer_1_out0));
  ROM #(.addrWidth(5), .dataWidth(32)) rom_2 (
    .addr(counter_1_out_4[4:0]), .data(rom_2_data), .sel(demultiplexer_1_out1));
  ROM #(.addrWidth(5), .dataWidth(32)) rom_3 (
    .addr(counter_1_out_4[4:0]), .data(rom_3_data), .sel(demultiplexer_1_out2));
  ROM #(.addrWidth(5), .dataWidth(32)) rom_4 (
    .addr(counter_1_out_4[4:0]), .data(rom_4_data), .sel(demultiplexer_1_out3));
  Multiplexer #(.select(2), .width(32)) multiplexer_1 (
    .in0(rom_1_data), .in1(rom_2_data), .in2(rom_3_data), .in3(rom_4_data), .out(out_4), .sel(ROM_Select));  // open: en
  Control_Unit control_unit_1 (
    .Clear(On_Off), .Input(out_4), .Clock(clock_1_out), .Jump(control_unit_1_jump),
    .JMP_Register(control_unit_1_jmp_register));  // open: ARAM_Register

  // Notes on the sheet:
  //   contents of rom_1 (hex, n*v repeats v):
  //   c20005 421890 4308d0 1c350c0 600000 1810
endmodule

module Counter (
  input  Clock,
  input  Store,
  input  [31:0] in_3,
  output [31:0] out_4
);

  wire not_1_out;
  wire [31:0] adder_1_out, multiplexer_1_out;

  not not_1 (not_1_out, Clock);
  Adder #(.width(32)) adder_1 (.a(out_4), .b(32'h1), .out(adder_1_out));  // open: cin, cout
  Multiplexer #(.width(32)) multiplexer_1 (
    .in0(adder_1_out), .in1(in_3), .out(multiplexer_1_out), .sel(Store));  // open: en
  Register #(.width(32)) register_1 (.D(multiplexer_1_out), .en(not_1_out), .Q(out_4), .clk(Clock));  // open: clr
endmodule

module PC (
  input  [1:0] Program_Select,
  input  Clear_Screen,
  input  Manual_Jump,
  input  On_Off
);

  wire clock_1_out;
  wire [31:0] executor_1_out_4;

  Executor executor_1 (
    .ManualJump(Manual_Jump), .On_Off(On_Off), .ROM_Select(Program_Select), .out_4(executor_1_out_4));
  TTY tty_1 (.data(executor_1_out_4[6:0]), .clk(clock_1_out), .we(On_Off), .clr(Clear_Screen));
  Clock clock_1 (.out(clock_1_out));
endmodule
