// Logisim project TwoHourCPU.circ as structural Verilog
module Full_Adder (
  input  A,
  input  B,
  input  C,
  output H,
  output L
);

  wire and_1_out, and_2_out, xor_1_out;

  xor xor_1 (xor_1_out, B, C);
  xor xor_2 (L, A, xor_1_out);
  and and_1 (and_1_out, A, xor_1_out);
  and and_2 (and_2_out, B, C);
  or or_1 (H, and_1_out, and_2_out);
endmodule

module DumbALU (
  input  [3:0] A,
  input  [3:0] B,
  input  [1:0] OP,
  output [3:0] out_4,
  output Carry
);

  wire multiplexer_3_out;
  wire [3:0] and_1_out, multiplexer_1_out, multiplexer_2_out, nand_1_out, not_1_out;
  wire [4:0] n4_bit_adder_1_out_4;

  assign not_1_out = ~B;  // NOT_Gate not_1, 4 bits wide
  assign nand_1_out = ~(A & B);  // NAND_Gate nand_1, 4 bits wide
  Multiplexer #(.select(2), .width(4), .enable("false")) multiplexer_1 (
    .in0(A), .in1(A), .in2(A), .in3(A), .out(multiplexer_1_out), .sel(OP));
  Multiplexer #(.select(2), .width(4), .enable("false")) multiplexer_2 (
    .in0(B), .in1(not_1_out), .in2(B), .in3(B), .out(multiplexer_2_out), .sel(OP));
  assign and_1_out = A & B;  // AND_Gate and_1, 4 bits wide
  Multiplexer #(.select(2), .enable("false")) multiplexer_3 (
    .in0(1'b0), .in1(1'b1), .in2(1'b0), .in3(1'b0), .out(multiplexer_3_out), .sel(OP));
  _4_Bit_Adder u_4_bit_adder_1 (
    .in_1(multiplexer_1_out), .in_2(multiplexer_2_out), .C(multiplexer_3_out), .out_4(n4_bit_adder_1_out_4));
  Multiplexer #(.select(2), .width(5), .enable("false")) multiplexer_4 (
    .in0(n4_bit_adder_1_out_4), .in1(n4_bit_adder_1_out_4), .in2({1'b0, and_1_out}),
    .in3({1'b0, nand_1_out}), .out({Carry, out_4}), .sel(OP));

  // Notes on the sheet:
  //   OP 00: add 01: sub 10: AND 11: NAND
  //   Carry Flag will always be on in sub, ignore it
endmodule

module _4_Bit_Adder (
  input  [3:0] in_1,
  input  [3:0] in_2,
  input  C,
  output [4:0] out_4
);

  wire full_adder_1_h, full_adder_2_h, full_adder_3_h;

  Full_Adder full_adder_1 (.A(in_1[0]), .B(in_2[0]), .C(C), .H(full_adder_1_h), .L(out_4[0]));
  Full_Adder full_adder_2 (.A(in_1[1]), .B(in_2[1]), .C(full_adder_1_h), .H(full_adder_2_h), .L(out_4[1]));
  Full_Adder full_adder_3 (.A(in_1[2]), .B(in_2[2]), .C(full_adder_2_h), .H(full_adder_3_h), .L(out_4[2]));
  Full_Adder full_adder_4 (.A(in_1[3]), .B(in_2[3]), .C(full_adder_3_h), .H(out_4[4]), .L(out_4[3]));
endmodule

module FinishedCPU (
);

  wire and_1_out, and_2_out, Cl, Clear, not_1_out, not_2_out, not_3_out, S, W;
  wire [1:0] OP;
  wire [3:0] A, B, counter_1_q, D, demultiplexer_1_out0, demultiplexer_1_out1, demultiplexer_2_out0,
       demultiplexer_2_out1, M, multiplexer_1_out, O;

  Button button_1 (.out(Clear));
  ROM #(.addrWidth(4), .dataWidth(12)) rom_1 (.addr(counter_1_q), .data({D, M, S, W, OP}), .sel(1'b1));
  Clock clock_1 (.out(Cl));
  Counter #(.width(4), .max('h2)) counter_1 (
    .load(Clear), .count(Cl), .Q(counter_1_q), .clk(Cl));  // open: D, carry, clr
  Multiplexer #(.width(4), .enable("false")) multiplexer_1 (.in0(O), .in1(D), .out(multiplexer_1_out), .sel(W));
  Demultiplexer #(.width(4), .enable("false")) demultiplexer_1 (
    .out0(demultiplexer_1_out0), .out1(demultiplexer_1_out1), .in(multiplexer_1_out), .sel(S));
  not not_1 (not_1_out, S);
  not not_2 (not_2_out, M[0]);
  not not_3 (not_3_out, S);
  Demultiplexer #(.width(4), .enable("false")) demultiplexer_2 (
    .out0(demultiplexer_2_out0), .out1(demultiplexer_2_out1), .in(demultiplexer_1_out0), .sel(M[0]));
  and and_1 (and_1_out, M[0], not_1_out);
  Register #(.width(4)) register_1 (.D(demultiplexer_2_out0), .en(and_2_out), .Q(A), .clk(Cl), .clr(Clear));
  and and_2 (and_2_out, not_2_out, not_3_out);
  DumbALU dumbalu_1 (.A(A), .B(B), .OP(OP), .out_4(O));  // open: Carry
  Register #(.width(4)) register_2 (.D(demultiplexer_2_out1), .en(and_1_out), .Q(B), .clk(Cl), .clr(Clear));
  RAM #(.addrWidth(4), .dataWidth(4), .bus("separate")) ram_1 (
    .addr(M), .din(demultiplexer_1_out1), .str(S), .sel(1'b1), .clk(Cl), .ld(1'b1), .clr(Clear));  // open: data

  // Other names for the same wires on the sheet: R = M[0]

  // Notes on the sheet:
  //   Program
  //   Bits 01 - Operation
  //   OP: Operation
  //   AB:Registers
  //   D: Data in third nibble
  //   R: Which Register
  //   O: ALU Output
  //   W: Write or Operate
  //   M: Address for RAM
  //   Bit 2 - Output bits 89AB Instead
  //   Bit 3 - Register or Address Select
  //   Bits 4567 - Address / Register
  //   Bits 89AB - Extra Write Stuff
  //   S: Select Register or RAM to write to
  //   contents of rom_1 (hex, n*v repeats v):
  //   304 214 8
  //   Demo Program
  //   304: Write 3 to A
  //   214: Write 2 to B
  //   008: Add AB, Out to RAM
  //   CPU
endmodule
